# Fritzing sketch Arduino_Uno_Scheme (saved by Fritzing 0.9.3b)
breadboards: 1

parts:
  U1 = ESP8266 WiFi Module [part_number=ESP8266]
  R5 = Resistor [tolerance=±5% resistance=10k package="2512 [SMD]"]
  LED1_-_Wifi = smd LED [color="Blue (505nm)" package="1206 [SMD]"]
  LED2_-_Busy = smd LED [color="Red (635nm)" package="1206 [SMD]"]
  R6 = Resistor [tolerance=±5% resistance=220 package="2512 [SMD]"]
  R7 = Resistor [tolerance=±5% resistance=100 package="2512 [SMD]"]
  Componente1 = Arduino Uno (Rev3)
  S3 = Momentary Switch [package=ksa_sealed_tac_switch]
  VCC1 = Battery block 9V

nets:
  N1: U1.RXD, Componente1.D11_PWM/MOSI
  VCC: U1.VCC, U1.CH_PD, Componente1.3V3
  GND: U1.GND, LED1_-_Wifi.cathode, LED2_-_Busy.cathode, Componente1.GND, S3.1, VCC1.-
  N2: U1.TXD, Componente1.D10_PWM/SS
  N3: R5.Pin_0, Componente1.D8, S3.3
  N4: R5.Pin_1, Componente1.5V
  N5: LED1_-_Wifi.anode, R7.Pin_0
  N6: LED2_-_Busy.anode, R6.Pin_0
  N7: R6.Pin_1, Componente1.D3_PWM
  N8: R7.Pin_1, Componente1.D4
  N9: Componente1.VIN, VCC1.+

custom parts:
  ESP8266 WiFi Module: Generic WiFi Module based on the ESP8266 with onboard PCB antenna and UART communications
